# Fritzing sketch GpioConsoleHost (saved by Fritzing 0.9.3b)
breadboards: 1

parts:
  Raspberry_Pi2 = Raspberry Pi B+
  LED1 = LED - 5mm [color="Red (633nm)" package="5 mm [THT]"]
  R2 = Resistor [tolerance=±5% resistance=470 package=THT]  # not connected
  J2 = Piezo Speaker
  LED2 = RGB LED (com. cathode, rgb) [package="5 mm [THT]"]
  R3 = Resistor [tolerance=±5% resistance=470 package=THT]
  R4 = Resistor [tolerance=±5% resistance=470 package=THT]
  R5 = Resistor [tolerance=±5% resistance=470 package=THT]

nets:
  N1: Raspberry_Pi2.GPIO17, R3.Pin_1
  N2: Raspberry_Pi2.GPIO27, R5.Pin_1
  N3: Raspberry_Pi2.GPIO16, J2.pin2
  N4: Raspberry_Pi2.GPIO23, LED1.anode
  N5: Raspberry_Pi2.GND, J2.pin1
  N6: Raspberry_Pi2.GPIO18, R4.Pin_1
  N7: LED2.red_anode, R3.Pin_0
  N8: LED2.green_anode, R4.Pin_0
  N9: LED2.blue_anode, R5.Pin_0
